# Fritzing sketch Wiring_Layout (saved by Fritzing 0.9.9b)
breadboards: 2

parts:
  Part1 = Arduino Uno (Rev3)
  Part2 = Digital FM Radio Receiver
  TRRS1 = Audio Jack (TRRS) 3.5mm [part_number="LUMBERG JEITA RC-5325A" package="RC-5325A [SMD]"]  # not connected
  Part3 = LCD1602-I2C
  SPKR1 = Loudspeaker
  AMP1 = PAM8403 6W Stereo Amplifier

nets:
  N1: Part1.A1, Part2.GND
  N2: Part1.A2, Part2.SDIO
  N3: Part1.A4/SDA, Part3.SDA
  N4: Part1.A5/SCL, Part3.SCL
  5V: Part1.5V, Part2.3.3V, Part3.VCC, AMP1.POWER+
  GND: Part1.GND, Part2.SCLK, Part3.GND, AMP1.POWER-
  N5: SPKR1.pin1, AMP1.ROUT-
  N6: SPKR1.pin2, AMP1.ROUT+

notes:
  TEA5767
  TEA5767 FM Radio Module
  16x2 LCD Display
  LM386 Audio Amplifier
  LM386
  Ignore rest of the pins that are not connected since you won't find them on the TEA5767 FM Radio Module

custom parts:
  LCD1602-I2C: A standard character display, usually with 2x16 characters. Comes in many colors with LCM1602 IIC attached.
  PAM8403 6W Stereo Amplifier: PAM8403 6 Watt Stereo Amplifier
